# Fritzing sketch charge (saved by Fritzing 1.0.1rc)
breadboards: 2

parts:
  Nano1 = Arduino Nano v2.3
  U1 = 74HC595 [package="DIP16 [THT]"]
  D1 = LED_BARGRAPH_10 [package=led_bargaph_10]
  R1 = Resistor [tolerance=±5% power=0.25W resistance=220 package=THT]
  R2 = Resistor [tolerance=±5% power=0.25W resistance=220 package=THT]
  R3 = Resistor [tolerance=±5% power=0.25W resistance=220 package=THT]
  R4 = Resistor [tolerance=±5% power=0.25W resistance=220 package=THT]
  R5 = Resistor [tolerance=±5% power=0.25W resistance=220 package=THT]
  R6 = Resistor [tolerance=±5% power=0.25W resistance=220 package=THT]
  R7 = Resistor [tolerance=±5% power=0.25W resistance=220 package=THT]
  R8 = Resistor [tolerance=±5% power=0.25W resistance=220 package=THT]
  R9 = Resistor [tolerance=±5% power=0.25W resistance=220 package=THT]
  U2 = 74HC595 [package="DIP16 [THT]"]
  D2 = LED_BARGRAPH_10 [package=led_bargaph_10]
  U3 = 74HC595 [package="DIP16 [THT]"]
  R11 = Resistor [tolerance=±5% power=0.25W resistance=220 package=THT]
  R12 = Resistor [tolerance=±5% power=0.25W resistance=220 package=THT]
  R13 = Resistor [tolerance=±5% power=0.25W resistance=220 package=THT]
  R14 = Resistor [tolerance=±5% power=0.25W resistance=220 package=THT]
  R15 = Resistor [tolerance=±5% power=0.25W resistance=220 package=THT]
  R16 = Resistor [tolerance=±5% power=0.25W resistance=220 package=THT]
  R17 = Resistor [tolerance=±5% power=0.25W resistance=220 package=THT]
  R18 = Resistor [tolerance=±5% power=0.25W resistance=220 package=THT]
  R19 = Resistor [tolerance=±5% power=0.25W resistance=220 package=THT]
  R20 = Resistor [tolerance=±5% power=0.25W resistance=220 package=THT]
  R21 = Resistor [tolerance=±5% power=0.25W resistance=220 package=THT]
  D3 = LED_BARGRAPH_10 [package=led_bargaph_10]
  D4 = LED_BARGRAPH_10 [package=led_bargaph_10]
  U4 = 74HC595 [package="DIP16 [THT]"]
  U5 = 74HC595 [package="DIP16 [THT]"]
  R22 = Resistor [tolerance=±5% power=0.25W resistance=220 package=THT]
  R23 = Resistor [tolerance=±5% power=0.25W resistance=220 package=THT]
  R24 = Resistor [tolerance=±5% power=0.25W resistance=220 package=THT]
  R25 = Resistor [tolerance=±5% power=0.25W resistance=220 package=THT]
  R26 = Resistor [tolerance=±5% power=0.25W resistance=220 package=THT]
  R27 = Resistor [tolerance=±5% power=0.25W resistance=220 package=THT]
  R28 = Resistor [tolerance=±5% power=0.25W resistance=220 package=THT]
  R29 = Resistor [tolerance=±5% power=0.25W resistance=220 package=THT]
  R30 = Resistor [tolerance=±5% power=0.25W resistance=220 package=THT]
  R31 = Resistor [tolerance=±5% power=0.25W resistance=220 package=THT]
  R32 = Resistor [tolerance=±5% power=0.25W resistance=220 package=THT]
  R33 = Resistor [tolerance=±5% power=0.25W resistance=220 package=THT]
  R34 = Resistor [tolerance=±5% power=0.25W resistance=220 package=THT]
  R35 = Resistor [tolerance=±5% power=0.25W resistance=220 package=THT]
  R36 = Resistor [tolerance=±5% power=0.25W resistance=220 package=THT]
  R37 = Resistor [tolerance=±5% power=0.25W resistance=220 package=THT]
  R38 = Resistor [tolerance=±5% power=0.25W resistance=220 package=THT]
  R39 = Resistor [tolerance=±5% power=0.25W resistance=220 package=THT]
  R40 = Resistor [tolerance=±5% power=0.25W resistance=220 package=THT]
  R41 = Resistor [tolerance=±5% power=0.25W resistance=220 package=THT]

nets:
  N1: Nano1.D2, U1.SH_CP, U2.SH_CP, U3.SH_CP
  N2: Nano1.D3, U1.ST_CP, U2.ST_CP, U3.ST_CP, U4.SH_CP, U4.ST_CP, U5.SH_CP, U5.ST_CP
  N3: Nano1.D4, U1.OE
  N4: Nano1.D5, U1.DS
  VCC: Nano1.+5V, U1.VCC, U2.VCC, U3.VCC, U4.VCC, U5.VCC
  GND: Nano1.GND, U1.GND, R1.Pin_1, R2.Pin_1, R3.Pin_1, R4.Pin_1, R5.Pin_1, R6.Pin_1, R7.Pin_1, R8.Pin_1, R9.Pin_1, U2.GND, U3.GND, R11.Pin_1, R12.Pin_1, R13.Pin_1, R14.Pin_1, R15.Pin_1, R16.Pin_1, R17.Pin_1, R18.Pin_1, R19.Pin_1, R20.Pin_1, R21.Pin_1, U4.GND, U5.GND, R22.Pin_1, R23.Pin_1, R24.Pin_1, R25.Pin_1, R26.Pin_1, R27.Pin_1, R28.Pin_1, R29.Pin_1, R30.Pin_1, R31.Pin_1, R32.Pin_1, R33.Pin_1, R34.Pin_1, R35.Pin_1, R36.Pin_1, R37.Pin_1, R38.Pin_1, R39.Pin_1, R40.Pin_1, R41.Pin_1
  N5: U1.Q1, D1.A_C
  N6: U1.Q2, D1.B_C
  N7: U1.Q3, D1.C_C
  N8: U1.Q4, D1.D_C
  N9: U1.Q5, D1.E_C
  N10: U1.Q6, D1.F_C
  N11: U1.Q7, D1.G_C
  N12: U1.Q7', U2.DS
  N13: U1.Q0, D1.H_C
  N14: D1.A_A, R1.Pin_0
  N15: D1.B_A, R2.Pin_0
  N16: D1.C_A, R4.Pin_0
  N17: D1.D_A, R3.Pin_0
  N18: D1.E_A, R7.Pin_0
  N19: D1.F_A, R8.Pin_0
  N20: D1.G_A, R6.Pin_0
  N21: D1.H_A, R5.Pin_0
  N22: D1.I_A, R9.Pin_0
  N23: D1.J_A, R11.Pin_0
  N24: D1.J_C, U2.Q2
  N25: D1.I_C, U2.Q1
  N26: U2.Q3, D2.A_C
  N27: U2.Q4, D2.B_C
  N28: U2.Q5, D2.C_C
  N29: U2.Q6, D2.D_C
  N30: U2.Q7, D2.E_C
  N31: U2.Q7', U3.DS
  N32: U2.OE, U3.OE, U4.OE
  N33: U2.Q0, D2.F_C
  N34: D2.A_A, R12.Pin_0
  N35: D2.B_A, R13.Pin_0
  N36: D2.C_A, R14.Pin_0
  N37: D2.D_A, R15.Pin_0
  N38: D2.E_A, R16.Pin_0
  N39: D2.F_A, R17.Pin_0
  N40: D2.G_A, R18.Pin_0
  N41: D2.H_A, R19.Pin_0
  N42: D2.I_A, R20.Pin_0
  N43: D2.J_A, R21.Pin_0
  N44: D2.J_C, U3.Q4
  N45: D2.I_C, U3.Q3
  N46: D2.H_C, U3.Q2
  N47: D2.G_C, U3.Q1
  N48: U3.Q5, D3.A_C
  N49: U3.Q6, D3.B_C
  N50: U3.Q7, D3.C_C
  N51: U3.Q7', U4.DS
  N52: U3.Q0, D3.D_C
  N53: D3.A_A, R22.Pin_0
  N54: D3.B_A, R23.Pin_0
  N55: D3.C_A, R24.Pin_0
  N56: D3.D_A, R25.Pin_0
  N57: D3.E_A, R26.Pin_0
  N58: D3.F_A, R27.Pin_0
  N59: D3.G_A, R28.Pin_0
  N60: D3.H_A, R29.Pin_0
  N61: D3.I_A, R30.Pin_0
  N62: D3.J_A, R31.Pin_0
  N63: D3.J_C, U4.Q6
  N64: D3.I_C, U4.Q5
  N65: D3.H_C, U4.Q4
  N66: D3.G_C, U4.Q3
  N67: D3.F_C, U4.Q2
  N68: D3.E_C, U4.Q1
  N69: D4.A_A, R32.Pin_0
  N70: D4.B_A, R33.Pin_0
  N71: D4.C_A, R34.Pin_0
  N72: D4.D_A, R35.Pin_0
  N73: D4.E_A, R36.Pin_0
  N74: D4.F_A, R37.Pin_0
  N75: D4.G_A, R38.Pin_0
  N76: D4.H_A, R39.Pin_0
  N77: D4.I_A, R40.Pin_0
  N78: D4.J_A, R41.Pin_0
  N79: D4.J_C, U5.Q0
  N80: D4.I_C, U5.Q7
  N81: D4.H_C, U5.Q6
  N82: D4.G_C, U5.Q5
  N83: D4.F_C, U5.Q4
  N84: D4.E_C, U5.Q3
  N85: D4.D_C, U5.Q2
  N86: D4.C_C, U5.Q1
  N87: D4.B_C, U4.Q0
  N88: D4.A_C, U4.Q7
  N89: U4.Q7', U5.DS
