# Fritzing sketch cyclotron (saved by Fritzing 1.0.1rc)
circuit board: 8.46667cm x 5.64444cm
breadboards: 2

parts:
  Part1 = Arduino Nano (Rev3.0)
  BAT1 = BC9VPC [package=bc9vpc]
  R1 = Resistor [tolerance=±5% resistance=180 package=THT]
  LED2 = smd LED [color="Red (633nm)" package="0805 [SMD]"]
  R2 = Resistor [tolerance=±5% resistance=180 power=0.25W package=THT]
  LED3 = smd LED [color="Red (633nm)" package="0805 [SMD]"]
  R3 = Resistor [tolerance=±5% resistance=180 power=0.25W package=THT]
  LED4 = smd LED [color="Red (633nm)" package="0805 [SMD]"]
  LED5 = smd LED [color="Red (633nm)" package="0805 [SMD]"]
  LED6 = smd LED [color="Red (633nm)" package="0805 [SMD]"]
  R4 = Resistor [tolerance=±5% resistance=180 power=0.25W package=THT]
  R5 = Resistor [tolerance=±5% resistance=180 power=0.25W package=THT]
  R6 = Resistor [tolerance=±5% resistance=180 power=0.25W package=THT]
  LED7 = smd LED [color="Red (633nm)" package="0805 [SMD]"]
  LED8 = smd LED [color="Red (633nm)" package="0805 [SMD]"]
  LED9 = smd LED [color="Red (633nm)" package="0805 [SMD]"]
  R7 = Resistor [tolerance=±5% resistance=180 power=0.25W package=THT]
  R8 = Resistor [tolerance=±5% resistance=180 power=0.25W package=THT]
  R9 = Resistor [tolerance=±5% resistance=180 power=0.25W package=THT]
  LED10 = smd LED [color="Red (633nm)" package="0805 [SMD]"]
  LED11 = smd LED [color="Red (633nm)" package="0805 [SMD]"]
  LED12 = smd LED [color="Red (633nm)" package="0805 [SMD]"]
  R10 = Resistor [tolerance=±5% resistance=180 power=0.25W package=THT]
  R11 = Resistor [tolerance=±5% resistance=180 power=0.25W package=THT]
  R12 = Resistor [tolerance=±5% resistance=180 power=0.25W package=THT]
  LED1 = smd LED [color="Red (633nm)" package="0805 [SMD]"]

nets:
  N1: Part1.GND, BAT1.V-, LED3.cathode, LED4.cathode, LED5.cathode, LED6.cathode, LED7.cathode, LED8.cathode, LED9.cathode, LED10.cathode, LED11.cathode, LED12.cathode, LED1.cathode
  N2: Part1.D3, R1.Pin_1, R2.Pin_1, R3.Pin_1
  N3: Part1.D5, R4.Pin_1, R5.Pin_1, R6.Pin_1
  N4: Part1.D6, R7.Pin_1, R8.Pin_1, R9.Pin_1
  N5: Part1.D9, R10.Pin_1, R11.Pin_1, R12.Pin_1
  N6: Part1.VIN, BAT1.V+
  N7: R1.Pin_0, LED1.anode
  N8: LED2.anode, R2.Pin_0
  N9: LED3.anode, R3.Pin_0
  N10: LED4.anode, R5.Pin_0
  N11: LED5.anode, R4.Pin_0
  N12: LED6.anode, R6.Pin_0
  N13: LED7.anode, R8.Pin_0
  N14: LED8.anode, R9.Pin_0
  N15: LED9.anode, R7.Pin_0
  N16: LED10.anode, R11.Pin_0
  N17: LED11.anode, R12.Pin_0
  N18: LED12.anode, R10.Pin_0
